// Logisim project masinacoca.circ as structural Verilog
module main (
  input  [2:0] in_1,
  input  in_2,
  output [3:0] out_3,
  output out_4
);

  wire clock_1_out;
  wire [0:0] undriven, undriven_2;
  wire [6:5] sevensegmentdecoder_1_output1, sevensegmentdecoder_1_output2;

  Clock clock_1 (.out(clock_1_out));
  sodamachine sodamachine_1 (.bills(in_1), .clk(clock_1_out), .reset(in_2), .\output (out_3), .std_err(out_4));
  SevenSegmentDecoder sevensegmentdecoder_1 (
    .Input(out_3), .output1({sevensegmentdecoder_1_output1, {5{sevensegmentdecoder_1_output1[6]}}}),
    .output2({sevensegmentdecoder_1_output2, {5{sevensegmentdecoder_1_output2[6]}}}));
  _7_Segment_Display u_7_segment_display_1 (
    .g(sevensegmentdecoder_1_output2[6]), .f(sevensegmentdecoder_1_output2[6]),
    .a(sevensegmentdecoder_1_output2[6]), .b(sevensegmentdecoder_1_output2[5]),
    .e(sevensegmentdecoder_1_output2[6]), .d(sevensegmentdecoder_1_output2[6]),
    .c(sevensegmentdecoder_1_output2[6]));  // open: dp
  _7_Segment_Display u_7_segment_display_2 (
    .g(undriven[0]), .f(sevensegmentdecoder_1_output2[6]), .a(sevensegmentdecoder_1_output2[5]),
    .b(sevensegmentdecoder_1_output2[6]), .e(sevensegmentdecoder_1_output2[6]),
    .d(sevensegmentdecoder_1_output2[6]), .c(sevensegmentdecoder_1_output2[6]),
    .dp(sevensegmentdecoder_1_output2[6]));
  _7_Segment_Display u_7_segment_display_3 (
    .g(sevensegmentdecoder_1_output1[6]), .f(sevensegmentdecoder_1_output1[6]),
    .a(sevensegmentdecoder_1_output1[6]), .b(sevensegmentdecoder_1_output1[5]),
    .e(sevensegmentdecoder_1_output1[6]), .d(sevensegmentdecoder_1_output1[6]),
    .c(sevensegmentdecoder_1_output1[6]));  // open: dp
  _7_Segment_Display u_7_segment_display_4 (
    .g(undriven_2[0]), .f(sevensegmentdecoder_1_output1[6]), .a(sevensegmentdecoder_1_output1[5]),
    .b(sevensegmentdecoder_1_output1[6]), .e(sevensegmentdecoder_1_output1[6]),
    .d(sevensegmentdecoder_1_output1[6]), .c(sevensegmentdecoder_1_output1[6]),
    .dp(sevensegmentdecoder_1_output1[6]));
endmodule

module newcirc (
  input  vreaurest,
  input  unleu,
  input  cincilei,
  input  zecelei,
  input  vreaucola,
  input  RESET,
  output [5:0] out_7,
  output out_8,
  output out_9,
  output out_10,
  output out_11
);

  wire calculator_1_error, CLK_out, undriven, undriven_2;
  wire [1:0] c2_1_output, c2_2_output, calculator_1_nr_bauturi;
  wire [3:0] calculator_1_output, counter_1_output;
  wire [6:0] sevensegmentdecoder_1_output1, sevensegmentdecoder_1_output2;

  Clock CLK (.out(CLK_out));
  counter counter_1 (.clk(unleu), .rst(RESET), .\output (counter_1_output));
  c2 c2_1 (.clk(cincilei), .rst(RESET), .\output (c2_1_output));
  c2 c2_2 (.clk(zecelei), .rst(RESET), .\output (c2_2_output));
  calculator calculator_1 (
    .\input ({zecelei, cincilei, unleu}), .clk(CLK_out), .reset(RESET), .vreaucola(vreaucola),
    .nr_bauturi(calculator_1_nr_bauturi), .\output (calculator_1_output), .error(calculator_1_error));
  d_ff d_ff_1 (.D(calculator_1_output[3]), .CLK(CLK_out), .RESET(RESET), .Q(out_8));
  d_ff d_ff_2 (.D(calculator_1_output[2]), .CLK(CLK_out), .RESET(RESET), .Q(out_9));
  LED led_1 (.in(undriven));
  LED led_2 (.in(undriven_2));
  d_ff d_ff_3 (.D(calculator_1_output[1]), .CLK(CLK_out), .RESET(RESET), .Q(out_10));
  SevenSegmentDecoder sevensegmentdecoder_1 (
    .Input({out_8, out_9, out_10, out_11}), .output1(sevensegmentdecoder_1_output1),
    .output2(sevensegmentdecoder_1_output2));
  LED led_3 (.in(calculator_1_error));
  d_ff d_ff_4 (.D(calculator_1_output[0]), .CLK(CLK_out), .RESET(RESET), .Q(out_11));
  _7_Segment_Display u_7_segment_display_1 (
    .g(sevensegmentdecoder_1_output2[0]), .f(sevensegmentdecoder_1_output2[1]),
    .a(sevensegmentdecoder_1_output2[6]), .b(sevensegmentdecoder_1_output2[5]),
    .e(sevensegmentdecoder_1_output2[2]), .d(sevensegmentdecoder_1_output2[3]),
    .c(sevensegmentdecoder_1_output2[4]));  // open: dp
  _7_Segment_Display u_7_segment_display_2 (
    .g(sevensegmentdecoder_1_output1[0]), .f(sevensegmentdecoder_1_output1[1]),
    .a(sevensegmentdecoder_1_output1[6]), .b(sevensegmentdecoder_1_output1[5]),
    .e(sevensegmentdecoder_1_output1[2]), .d(sevensegmentdecoder_1_output1[3]),
    .c(sevensegmentdecoder_1_output1[4]));  // open: dp
endmodule

// VHDL entity sodamachine, as the project stores it:
--------------------------------------------------------------------------------
-- Project :soda machine for PCLP4_1
-- File    :
-- Autor   :Armega Andrei
-- Date    :11/3/2023
--
--------------------------------------------------------------------------------
-- Description :
--
--------------------------------------------------------------------------------

LIBRARY ieee;
USE ieee.std_logic_1164.all;

ENTITY sodamachine IS
  PORT (
       bills : in std_logic_vector(2 downto 0);
       output: out std_logic_vector(3 downto 0);
       std_err : out std_logic;
       clk,reset:in std_logic
    );
END sodamachine;



ARCHITECTURE TypeArchitecture OF sodamachine IS
signal nxstate : std_logic_vector(3 downto 0):= "0000";
signal curstate : std_logic_vector(3 downto 0):= "0000";
signal intermediary_err :std_logic :='0';
signal intermediary_output:std_logic_vector(3 downto 0):="0000";

BEGIN

process(nxstate)
begin

    curstate<=nxstate;
     intermediary_output<= nxstate;
    
end process;

process(clk,reset,nxstate)
begin

--if(reset ='1') then curstate<="0000";end if;

case curstate is 

when "0000" => intermediary_output <= curstate;
 if (bills = "001" ) then nxstate <= "0001";intermediary_err  <='0';
 elsif (bills = "010" ) then nxstate <="0101"; intermediary_err  <='0';
 elsif (bills = "100" ) then nxstate <= "1010";intermediary_err  <='0';
 end if; 

when "0001" => intermediary_output <= curstate;

 if(bills ="001") then nxstate <= "0010"; intermediary_err  <='0';
 elsif(bills = "010") then nxstate <= "0110";intermediary_err  <='0';
 elsif(bills = "100") then nxstate <= "1011";intermediary_err  <='0';
 end if;

 when "0010" =>intermediary_output <= curstate;
 if(bills ="001") then nxstate <= "0011";intermediary_err  <='0';
 elsif(bills = "010") then nxstate <= "0111";intermediary_err  <='0';
 elsif(bills = "100") then nxstate <= "1100";intermediary_err  <='0';
 end if;
 
 when "0011" =>intermediary_output <= curstate;
 if(bills ="001") then nxstate <= "0100";intermediary_err  <='0';
 elsif(bills = "010") then nxstate <= "1000";intermediary_err  <='0';
 elsif(bills = "100") then nxstate <= "1101";intermediary_err  <='0';
 end if;

 when "0100" =>intermediary_output <= curstate;
 if(bills ="001") then nxstate <= "0101";intermediary_err  <='0';
 elsif(bills = "010") then nxstate <= "1001";intermediary_err  <='0';
 elsif(bills = "100") then nxstate <= "1110";intermediary_err  <='0';
 end if;

when "0101" =>intermediary_output <= curstate;
 if(bills ="001") then nxstate <= "0110";intermediary_err  <='0';
 elsif(bills = "010") then nxstate <= "1010";intermediary_err  <='0';
 elsif(bills = "100") then nxstate <= "1111";intermediary_err  <='0';
 end if;

 when "0110" =>intermediary_output <= curstate;
 if(bills ="001") then nxstate <= "0111";intermediary_err  <='0';
 elsif(bills = "010") then nxstate <= "1011";intermediary_err  <='0';
 elsif(bills = "100") then nxstate <= "0110"; intermediary_err  <='1';
 end if;

  when "0111" =>intermediary_output <= curstate;
 if(bills ="001") then nxstate <= "1000";intermediary_err  <='0';
 elsif(bills = "010") then nxstate <= "1100";intermediary_err  <='0';
 elsif(bills = "100") then nxstate <= "0111"; intermediary_err  <='1';
 end if;

 when "1000" =>intermediary_output <= curstate;
 if(bills ="001") then nxstate <= "1001";intermediary_err  <='0';
 elsif(bills = "010") then nxstate <= "1101";intermediary_err  <='0';
 elsif(bills = "100") then nxstate <= "1000"; intermediary_err  <='1';
 end if;

 when "1001" =>intermediary_output <= curstate;
 if(bills ="001") then nxstate <= "1010";intermediary_err  <='0';
 elsif(bills = "010") then nxstate <= "1110";intermediary_err  <='0';
 elsif(bills = "100") then nxstate <= "1001"; intermediary_err  <='1';
 end if;

when "1010" =>intermediary_output <= curstate;
 if(bills ="001") then nxstate <= "1011";intermediary_err  <='0';
 elsif(bills = "010") then nxstate <= "1111";intermediary_err  <='0';
 elsif(bills = "100") then nxstate <= "1010"; intermediary_err  <='1';
 end if;

when "1011" =>intermediary_output <= curstate;
 if(bills ="001") then nxstate <= "1100";intermediary_err  <='0';
 elsif(bills = "010") then nxstate <= "1011";intermediary_err  <='1';
 elsif(bills = "100") then nxstate <= "1011"; intermediary_err  <='1';
 end if;

when "1100" =>intermediary_output <= curstate;
 if(bills ="001") then nxstate <= "1101";intermediary_err  <='0';
 elsif(bills = "010") then nxstate <= "1100";intermediary_err  <='1';
 elsif(bills = "100") then nxstate <= "1100"; intermediary_err  <='1';
 end if;

when "1101" =>intermediary_output <= curstate;
 if(bills ="001") then nxstate <= "1110";intermediary_err  <='0';
 elsif(bills = "010") then nxstate <= "1101";intermediary_err  <='1';
 elsif(bills = "100") then nxstate <= "1101"; intermediary_err  <='1';
 end if;

when "1110" =>intermediary_output <= curstate;
 if(bills ="001") then nxstate <= "1111";intermediary_err  <='0';
 elsif(bills = "010") then nxstate <= "1110";intermediary_err  <='1';
 elsif(bills = "100") then nxstate <= "1110"; intermediary_err  <='1';
 end if;

 when "1111" =>intermediary_output <= curstate;
 if(bills ="001") then nxstate <= "1111";intermediary_err  <='1';
 elsif(bills = "010") then nxstate <= "1111";intermediary_err  <='1';
 elsif(bills = "100") then nxstate <= "1111"; intermediary_err  <='1';
 end if;


 --------------
 when others => nxstate<= "0000";
 
end case;
output <= intermediary_output;
std_err <=intermediary_err ;

end process;

END TypeArchitecture;

// VHDL entity SevenSegmentDecoder, as the project stores it:
library ieee;
use ieee.std_logic_1164.all;
use ieee.numeric_std.all;

entity SevenSegmentDecoder is
  port (
    Input: in std_logic_vector(3 downto 0);
    
    output1 : out std_logic_vector(6 downto 0);
    output2 :out std_logic_vector(6 downto 0)

  );
end entity SevenSegmentDecoder;

architecture Behavioral of SevenSegmentDecoder is
begin

  process(Input)
    variable Value0: integer range 0 to 15;
   
  begin
    Value0 := to_integer(unsigned(Input(3 downto 0)));
   
    
    case Value0 is
      when 0 => output1 <= "1111110"; output2 <= "1111110";
      when 1 => output1 <= "0110000";output2 <= "1111110";
      when 2 => output1 <= "1101101";output2 <= "1111110";
      when 3 => output1 <= "1111001";output2 <= "1111110";
      when 4 => output1 <= "0110011";output2 <= "1111110";
      
      when 5 => output1 <= "1011011";output2 <= "1111110";
      when 6 => output1 <= "1011111";output2 <= "1111110";
      
      when 7 => output1 <= "1110000";output2 <= "1111110";
      when 8 => output1 <= "1111111";output2 <= "1111110";
      when 9 => output1 <= "1111011";output2 <= "1111110";
      
      when 10 => output2 <= "0110000"; output1 <= "1111110";
      when 11 => output2 <="0110000"; output1 <="0110000";
      when 12 => output2 <="0110000"; output1 <="1101101";
      when 13 =>output2 <="0110000"; output1 <="1111001";
      when 14 =>output2<="0110000";output1 <="0110011";
      when 15=>output2<="0110000";output1 <="1011011";

      
    end case;
    end process;
    end architecture;

// VHDL entity d_ff, as the project stores it:
LIBRARY ieee;
USE ieee.std_logic_1164.all;

ENTITY d_ff IS
  PORT (
  D,CLK ,RESET: in std_logic;
  Q:out std_logic
    );
END d_ff;


ARCHITECTURE TypeArchitecture OF d_ff IS

BEGIN

process(CLK,RESET)
begin


if(rising_edge(clk)) then if(RESET ='1') then

Q<='0';
else
Q<=D;
end if;
end if;
end process;

END TypeArchitecture;

// VHDL entity calculator, as the project stores it:
LIBRARY ieee;
USE ieee.std_logic_1164.all;
use IEEE.STD_LOGIC_ARITH.ALL;
use IEEE.STD_LOGIC_UNSIGNED.ALL; 

ENTITY calculator IS
  PORT (
   input : in std_logic_vector(2 downto 0);
   clk ,reset,vreaucola: in std_logic;
   nr_bauturi:out std_logic_vector(1 downto 0);
   output :out std_logic_vector(3 downto 0);
   error :out std_logic
    );
END calculator;

ARCHITECTURE TypeArchitecture OF calculator IS

BEGIN
 process(input,reset,vreaucola)
variable intern : std_logic_vector(4 downto 0) := "00000";
variable nr :std_logic_vector(1 downto 0) := "00";
variable err:std_logic := '0';
 begin
  if ( reset = '1') then intern := "00000" ;nr :="00"; end if;
  
  if( input ="001" and intern < "01111") then intern := intern + "00001";err :='0';
  elsif ( input ="001" and "00001" + intern > "01111") 
  then err :='1'; end if;
  
  if(input ="010"and intern < "01011") then intern := intern +"00101";err :='0';
    elsif ( input ="010" and "00101" + intern > "01111") 
    then err :='1'; end if;
  
  if(input ="100"and intern < "00110") then intern := intern + "01010" ;err :='0';
 elsif ( input ="100" and "01010" + intern > "01111")
 then err :='1'; end if;
  
  if (vreaucola ='1' AND intern > 2) then 
  intern := intern - "00011";
  nr := nr + "01"; end if;
  
  output <= intern(3)&intern(2)&intern(1)&intern(0);
  nr_bauturi <= nr;
  error <= err;
 end process;

END TypeArchitecture;

// VHDL entity and4, as the project stores it:
LIBRARY ieee;
USE ieee.std_logic_1164.all;

ENTITY and4 IS
  PORT (
   input : in std_logic_vector(3 downto 0);
   output : out std_logic
    );
END and4;



ARCHITECTURE TypeArchitecture OF and4 IS

BEGIN
  output <= input(3) and input(2) and input(1) and input(0);

END TypeArchitecture;

// VHDL entity and2, as the project stores it:
--------------------------------------------------------------------------------
-- Project :
-- File    :
-- Autor   :
-- Date    :
--
--------------------------------------------------------------------------------
-- Description :
--
--------------------------------------------------------------------------------

LIBRARY ieee;
USE ieee.std_logic_1164.all;

ENTITY and2 IS
  PORT (
 a,b : in std_logic;
 c:out std_logic
    );
END and2;

--------------------------------------------------------------------------------
--Complete your VHDL description below
--------------------------------------------------------------------------------

ARCHITECTURE TypeArchitecture OF and2 IS

BEGIN
c<=a and b;

END TypeArchitecture;

// VHDL entity or3, as the project stores it:
LIBRARY ieee;
USE ieee.std_logic_1164.all;

ENTITY or3 IS
  PORT (
  a,b,c  : in std_logic;
  d: out std_logic
    );
END or3;



ARCHITECTURE TypeArchitecture OF or3 IS

BEGIN
d <= a or b or c ;

END TypeArchitecture;

// VHDL entity counter, as the project stores it:
LIBRARY ieee;
USE ieee.std_logic_1164.all;
use IEEE.STD_LOGIC_ARITH.all;
use IEEE.STD_LOGIC_UNSIGNED.all;
ENTITY counter IS
  PORT (
     clk ,rst : in std_logic;
    output : out std_logic_vector(3 downto 0)
    );
END counter;
ARCHITECTURE TypeArchitecture OF counter IS
BEGIN
process (clk,rst)
variable counting : std_logic_vector(3 downto 0) := "0000";
begin
 if (rst = '1') then counting := "0000";
elsif(rising_edge(clk)) then
counting := counting + '1';
end if;
output <= counting;
end process;
END TypeArchitecture;

// VHDL entity secondcalculator, as the project stores it:
LIBRARY ieee;
USE ieee.std_logic_1164.all;
use IEEE.STD_LOGIC_ARITH.ALL;
use IEEE.STD_LOGIC_UNSIGNED.ALL; 

ENTITY secondcalculator IS
  PORT (
     clk: in std_logic;
     catcola : in std_logic_vector(1 downto 0);
      input : in std_logic_vector(8 downto 0);
     
      ledrosu,ledverde : out std_logic;
      output :out std_logic_vector(5 downto 0)
    );
END secondcalculator;

ARCHITECTURE TypeArchitecture OF secondcalculator IS
BEGIN
process(input,clk)
variable cati_bani_de_cola : std_logic_vector(3 downto 0) := "0000";
variable number_of_drinks : std_logic_vector(1 downto 0) :="00";
--variable cat_rest : std_logic_vector(3 downto 0) := "0000";
--variable temp :std_logic_vector(3 downto 0) := "0000";
--variable temp2 :std_logic_vector(3 downto 0) := "0000";
--variable rest_optim :std_logic_vector (7 downto 0) :="00000000";
--variable rest_neoptim :std_logic_vector (7 downto 0) :="00000000";
--variable cnt :std_logic_vector  (1 downto 0) :="00";
--variable cnt2 :std_logic_vector  (3 downto 0) :="0000";
--variable copie_cat_rest :std_logic_vector( 3 downto 0) := "0000";
variable inputandcola : std_logic_vector(10 downto 0) := "00000000000";

begin
if(input = "000000000") then 
ledverde <='0'; ledrosu <='0'; 
end if;

if(input /= "000000000") then
inputandcola := catcola(1 downto 0) & input(7 downto 0);
end if;

case inputandcola is 
when "00000000000" =>  ledverde <='0'; ledrosu <='0';
when "00000000001" =>  ledverde <='1';ledrosu <='0'; --1
when "00000000010" =>  ledverde <='1';ledrosu <='0';--2
when "00000000011" =>  ledverde <='1';ledrosu <='0';--3
when "00000000100" =>  ledverde <='1';ledrosu <='0';--4

when "00000100000" =>  ledverde <='1';ledrosu <='0';--5
when "00000000101" =>  ledverde <='1';ledrosu <='0';--5

when "00000100001" =>  ledverde <='1';ledrosu <='0';--6
when "00000000110" =>  ledverde <='1';ledrosu <='0';--6

when "00000000111" =>  ledverde <='1';ledrosu <='0';--7
when "00000100010" =>  ledverde <='1';ledrosu <='0';--7

when "00000001000" =>  ledverde <='1';ledrosu <='0';--8
when "00000100011" => ledverde <='1';ledrosu <='0';--8

when "00000100100" =>  ledverde <='1';ledrosu <='0';--9
when "00000001001" =>  ledverde <='1';ledrosu <='0';--9

when "00000100101" =>  ledverde <='1';ledrosu <='0';--10
when "00000001010" =>  ledverde <='1';ledrosu <='0';--10
when "00010000000" =>  ledrosu <='1';ledverde <='0';--10
when "00001000000" =>  ledverde <='1';ledrosu <='0';--10

when "00010000001" =>  ledverde <='1';ledrosu <='0';--11
when "00001000001" =>  ledverde <='1';ledrosu <='0';--11
when "00000001011" =>  ledverde <='1';ledrosu <='0';--11
when "00000100110" =>  ledverde <='1';ledrosu <='0';--11

when "00000001100" =>  ledverde <='1';ledrosu <='0';--12
when "00010000010" =>  ledverde <='1';ledrosu <='0';--12
when "00001000010" =>  ledverde <='1';ledrosu <='0';--12
when "00000100111" => ledverde <='1';ledrosu <='0';--12

when "00000001101" =>  ledverde <='1';ledrosu <='0';--13
when "00010000011" =>  ledverde <='1';ledrosu <='0';--13
when "00001000011" =>  ledverde <='1';ledrosu <='0';--13
when "00000101000" =>  ledverde <='1';ledrosu <='0';--13

when "00010000100" =>  ledverde <='1';ledrosu <='0';--14
when "00001000100" =>  ledverde <='1';ledrosu <='0';--14
when "00000001110" =>  ledverde <='1';ledrosu <='0';--14
when "00000101001" =>  ledverde <='1';ledrosu <='0';--14

when "00010000101" =>  ledverde <='1';ledrosu <='0';--15
when "00010100000" =>  ledverde <='1';ledrosu <='0';--15
when "00001100000" =>  ledverde <='1';ledrosu <='0';--15
when "00000001111" =>  ledverde <='1';ledrosu <='0';--15
when "00001000101" =>  ledverde <='1';ledrosu <='0';--15
when "00000101010" =>  ledverde <='1';ledrosu <='0';--15

------------------------------------------------

when "01000000100" =>  ledverde <='1';--4

when "01000100000" =>  ledverde <='0'; ledrosu<='1';--5
when "01000000101" =>   ledverde <='1'; ledrosu<='0';--5

when "01000100001" =>  ledverde <='0'; ledrosu<='1';--6
when "01000000110" =>  ledverde <='1'; ledrosu<='0';--6

when "01000000111" =>  ledverde <='1'; ledrosu<='0';--7
when "01000100010" =>  ledverde <='0'; ledrosu<='1';--7

when "01000001000" =>  ledverde <='1'; ledrosu<='0';--8
when "01000100011" => ledverde <='1'; ledrosu <='0';--8

when "01000100100" =>  ledverde <='1'; ledrosu<='0';--9
when "01000001001" =>  ledverde <='1'; ledrosu<='0';--9

when "01000100101" =>  ledverde <='1'; ledrosu<='0';--10
when "01000001010" =>  ledverde <='1'; ledrosu<='0';--10
when "01010000000" =>  ledrosu <='1';ledverde<='0'; --10
when "01001000000" =>  ledverde <='0'; ledrosu<='1';--10

when "01010000001" =>  ledverde <='0'; ledrosu<='1';--11
when "01001000001" => ledverde <='0'; ledrosu<='1';--11
when "01000001011" =>  ledverde <='1'; ledrosu<='0';--11
when "01000100110" =>  ledverde <='1'; ledrosu<='0';--11

when "01000001100" =>  ledverde <='1'; ledrosu<='0';--12
when "01010000010" => ledverde <='0'; ledrosu<='1';--12
when "01001000010" =>  ledverde <='0'; ledrosu<='1';--12
when "01000100111" => ledverde <='1'; ledrosu<='0';--12

when "01000001101" =>  ledverde <='1'; ledrosu<='0';--13
when "01010000011" =>  ledverde <='1'; ledrosu<='0';--13
when "01001000011" =>  ledverde <='1'; ledrosu<='0';--13
when "01000101000" =>  ledverde <='1'; ledrosu<='0';--13

when "01010000100" =>  ledverde <='1'; ledrosu<='0';--14
when "01001000100" =>  ledverde <='1'; ledrosu<='0';--14
when "01000001110" =>  ledverde <='1'; ledrosu<='0';--14
when "01000101001" =>  ledverde <='1'; ledrosu<='0';--14

when "01010000101" =>  ledverde <='1'; ledrosu<='0';--15
when "01010100000" =>  ledverde <='0'; ledrosu<='1';--15
when "01001100000" =>  ledverde <='0'; ledrosu<='1';--15
when "01000001111" =>  ledverde <='1'; ledrosu<='0';--15
when "01001000101" =>  ledverde <='1'; ledrosu<='0';--15
when "01000101010" =>  ledverde <='1'; ledrosu<='0';--15



--------------------------------------
when "10000000111" =>  ledverde <='1'; ledrosu<='0';--7
when "10000100010" =>  ledverde <='1'; ledrosu<='0';--7

when "10000001000" =>  ledverde <='1'; ledrosu<='0';--8 r2
when "10000100011" => ledverde <='1'; ledrosu <='0';--8 r2

when "10000100100" =>  ledverde <='1'; ledrosu<='0';--9 r 3
when "10000001001" =>  ledverde <='1'; ledrosu<='0';--9 

when "10000100101" =>  ledverde <='1'; ledrosu<='0';--10 r4
when "10000001010" =>  ledverde <='1'; ledrosu<='0';--10
when "10010000000" =>  ledrosu <='1';ledverde<='0' ;--10
when "10001000000" =>  ledverde <='0'; ledrosu<='1';--10

when "10010000001" =>  ledverde <='0'; ledrosu<='1';--11 r5
when "10001000001" => ledverde <='1'; ledrosu<='0';--11
when "10000001011" =>  ledverde <='1'; ledrosu<='0';--11
when "10000100110" =>  ledverde <='1'; ledrosu<='0';--11


when "10000001100" =>  ledverde <='1'; ledrosu<='0';--12 r6
when "10010000010" => ledverde <='0'; ledrosu<='1';--12
when "10001000010" =>  ledverde <='1'; ledrosu<='0';--12
when "10000100111" => ledverde <='1'; ledrosu<='0';--12

when "10000001101" =>  ledverde <='1'; ledrosu<='0';--13 r7
when "10010000011" =>  ledverde <='0'; ledrosu<='1';--13
when "10001000011" =>  ledverde <='1'; ledrosu<='0';--13
when "10000101000" =>  ledverde <='1'; ledrosu<='0';--13

when "10010000100" =>  ledverde <='0'; ledrosu<='1';--14 r8
when "10001000100" =>  ledverde <='1'; ledrosu<='0';--14
when "10000001110" =>  ledverde <='1'; ledrosu<='0';--14
when "10000101001" =>  ledverde <='1'; ledrosu<='0';--14

when "10010000101" =>  ledverde <='0'; ledrosu<='1';--15 r9
when "10010100000" =>  ledverde <='0'; ledrosu<='1';--15
when "10001100000" =>  ledverde <='0'; ledrosu<='1';--15
when "10000001111" =>  ledverde <='1'; ledrosu<='0';--15
when "10001000101" =>  ledverde <='1'; ledrosu<='0';--15
when "10000101010" =>  ledverde <='1'; ledrosu<='0';--15

--------------------------------------------------------

when "01001100001" =>  ledverde <='0'; ledrosu <='1'; --16 r13 5 5 5 1
when "01010100001" =>  ledverde <='0'; ledrosu<='1';--16  10 5 1
when "01010000110" =>   ledverde <='1'; ledrosu<='0';--16 10 6
when "01000101011" =>   ledverde <='1'; ledrosu<='0';--16 5 11




when others => ledrosu <='0'; ledverde<='0';
end case;



end process;



END TypeArchitecture;

// VHDL entity c2, as the project stores it:
LIBRARY ieee;
USE ieee.std_logic_1164.all;

use IEEE.STD_LOGIC_ARITH.all;
use IEEE.STD_LOGIC_UNSIGNED.all;
ENTITY c2 IS
  PORT (
     clk ,rst : in std_logic;
    output : out std_logic_vector(1 downto 0)
    );
END c2;
ARCHITECTURE TypeArchitecture OF c2 IS
BEGIN
process (clk,rst)
variable counting : std_logic_vector(1 downto 0) := "00";
begin
 if (rst = '1') then counting := "00";
elsif(rising_edge(clk)) then
counting := counting + '1';
end if;
output <=counting;
end process;
END TypeArchitecture;

// VHDL entity c1, as the project stores it:
LIBRARY ieee;
USE ieee.std_logic_1164.all;

use IEEE.STD_LOGIC_ARITH.all;
use IEEE.STD_LOGIC_UNSIGNED.all;
ENTITY c1 IS
  PORT (
     clk ,rst : in std_logic;
    output : out std_logic
    );
END c1;
ARCHITECTURE TypeArchitecture OF c1 IS
BEGIN
process (clk,rst)
variable counting : std_logic := '0';
begin
 if (rst = '1') then counting := '0';
elsif(rising_edge(clk)) then
counting := '1';
end if;
output <= counting;
end process;
END TypeArchitecture;

// VHDL entity or4, as the project stores it:
LIBRARY ieee;
USE ieee.std_logic_1164.all;

ENTITY or4 IS
  PORT (
  a,b,c ,e : in std_logic;
  d: out std_logic
    );
END or4;



ARCHITECTURE TypeArchitecture OF or4 IS

BEGIN

d <= a or b or c or e;

END TypeArchitecture;
