// Logisim project nou_design.circ as structural Verilog
module main (
  input  RESETptDEV,
  input  [2:0] BANCNOTE,
  input  COLA3lei,
  input  PEPSI4lei,
  input  REST,
  output [5:0] bancnotede1,
  output [5:0] bancnotede5,
  output bancnota5,
  output bancnota1,
  output cola1,
  output cola2,
  output [3:0] CREDIT,
  output out_13
);

  wire alu_1_disable, alu_1_semnal_reset, clock_1_out, d_ff_1_q, frequencydivider_1_clk_1hz,
       registru_bancnote_1_ledrosu, registru_bancnote_1_ledverde;
  wire [3:0] alu_1_output_request, calculator_1_to_register, decodificator_1_semnal_out;

  Clock clock_1 (.out(clock_1_out));
  decodificator decodificator_1 (
    .input1(BANCNOTE[0]), .input2(BANCNOTE[1]), .input3(BANCNOTE[2]), .semnal_out(decodificator_1_semnal_out));
  registru_bancnote registru_bancnote_1 (
    .reset(RESETptDEV), .input_bancnote(calculator_1_to_register), .bancnote_request(alu_1_output_request),
    .resurse1(bancnotede1), .resurse5(bancnotede5), .bancnote_5_out(bancnota5), .bancnote_1_out(bancnota1),
    .ledverde(registru_bancnote_1_ledverde), .ledrosu(registru_bancnote_1_ledrosu));
  calculator calculator_1 (
    .\input (decodificator_1_semnal_out), .reset(alu_1_semnal_reset), .vreaucola(COLA3lei),
    .vreaucola2(PEPSI4lei), .vreaurest(REST), .enable(alu_1_disable), .cola_1(cola1), .cola_2(cola2),
    .\output (CREDIT), .to_register(calculator_1_to_register), .error(out_13));
  FrequencyDivider frequencydivider_1 (.Clock(clock_1_out), .clk_1hz(frequencydivider_1_clk_1hz));
  d_ff d_ff_1 (.D(REST), .CLK(clock_1_out), .Q(d_ff_1_q));
  LED led_1 (.in(registru_bancnote_1_ledverde));
  LED led_2 (.in(registru_bancnote_1_ledrosu));
  ALU alu_1 (
    .clk(frequencydivider_1_clk_1hz), .vreaurest(d_ff_1_q), .OK(registru_bancnote_1_ledverde),
    .input_credit(CREDIT), .output_request(alu_1_output_request), .semnal_reset(alu_1_semnal_reset),
    .\disable (alu_1_disable));
endmodule

module tester (
  input  [2:0] BANCNOTE,
  input  COLA3lei,
  input  PEPSI4lei,
  input  REST,
  input  RESETDEV,
  output [5:0] bancnotede1,
  output [5:0] bancnotede5,
  output bancnota5,
  output bancnota1,
  output cola1,
  output cola2,
  output ERR,
  output [3:0] CREDIT
);

  wire clock_1_out, main_vending_1_nu_se_poate_da_rest, main_vending_1_se_poate_da_rest;

  Clock clock_1 (.out(clock_1_out));
  main_vending main_vending_1 (
    .bancnota_1_leu(BANCNOTE[0]), .bancnota_5_leu(BANCNOTE[1]), .bancnota_10_leu(BANCNOTE[2]),
    .cola(COLA3lei), .pepsi(PEPSI4lei), .clk(clock_1_out), .rest(REST), .RESETDEV(RESETDEV),
    .bancnote_5_in_memorie(bancnotede1), .bancnote_1_in_memorie(bancnotede5),
    .rest5_catre_utilizator(bancnota5), .rest1_catre_utilizator(bancnota1),
    .se_poate_da_rest(main_vending_1_se_poate_da_rest),
    .nu_se_poate_da_rest(main_vending_1_nu_se_poate_da_rest), .eliberare_cola(cola1),
    .eliberare_pepsi(cola2), .respingere_bancnota(ERR), .credit(CREDIT));
  LED led_1 (.in(main_vending_1_se_poate_da_rest));
  LED led_2 (.in(main_vending_1_nu_se_poate_da_rest));
endmodule

// VHDL entity decodificator, as the project stores it:
LIBRARY ieee;
USE ieee.std_logic_1164.all;

ENTITY decodificator IS
  PORT (
    input1,input2,input3 : in std_logic;
    semnal_out : out std_logic_vector (3 downto 0)
    );
END decodificator;


ARCHITECTURE TypeArchitecture OF decodificator IS

BEGIN

process(input1,input2,input3)
variable to_out: std_logic_vector (3 downto 0) := "0000";
begin


if( input1 = '1' AND  input2 ='0' AND input3 ='0') then
to_out := "0001";
elsif (input1 ='0'AND input2 = '1' AND input3 ='0') then
to_out :="0101";
elsif (input1 ='0' AND input2 = '0' AND input3 ='1')then
to_out :="1010";
elsif (input1 ='0' AND input2 = '0' AND input3 ='0')then
to_out:="0000";
end if;
semnal_out <= to_out;
end process;

END TypeArchitecture;

// VHDL entity calculator, as the project stores it:
LIBRARY ieee;
USE ieee.std_logic_1164.all;
use IEEE.STD_LOGIC_ARITH.ALL;
use IEEE.STD_LOGIC_UNSIGNED.ALL;

ENTITY calculator IS
  PORT (
 input : in std_logic_vector(3 downto 0);
   reset,vreaucola,vreaucola2,vreaurest,enable: in std_logic;
   cola_1 ,cola_2:out std_logic;
   output ,to_register:out std_logic_vector(3 downto 0);
   error :out std_logic
    );
END calculator;


ARCHITECTURE TypeArchitecture OF calculator IS

BEGIN
process(input,reset,vreaucola,vreaucola2,vreaurest)
variable intern : std_logic_vector(4 downto 0) := "00000";
variable std_err:std_logic :='0';
variable cola1 :std_logic :='0';
variable cola2 :std_logic :='0';
variable nr_bauturi : integer :=0;
variable req : std_logic_vector (3 downto 0) := "0000";
variable to_reg : std_logic_vector (3 downto 0) :="0000";
begin
if(input /= "0000" AND enable ='0') then std_err := '1'; end if;

if(input + intern < "10000" AND enable ='1') then intern := intern +input;cola1 :='0'; cola2:='0'; std_err :='0';to_reg := input;
elsif (input+intern >"01111") then std_err :='1'; 
else std_err :='0'; end if;

if( vreaucola ='1' AND intern > "00010" AND vreaucola2 ='0' AND reset ='0'  AND enable ='1') 
then intern := intern - "00011";
cola1 :='1';cola2:='0';
nr_bauturi := nr_bauturi+1; 
std_err :='0';
end if;

if( vreaucola2 ='1' AND intern > "00011" AND vreaucola ='0' AND reset ='0'  AND enable ='1') 
then intern := intern - "00100";
cola2 :='1'; cola1:='0';
nr_bauturi := nr_bauturi+1;
std_err :='0';
end if;

if(reset ='1') 
then intern :="00000"; 
cola1 :='0'; cola2 :='0';
std_err :='0';	
end if;

 if( vreaurest = '1'AND vreaucola2 ='0' AND vreaucola='0'  AND nr_bauturi =0 AND intern > "01001") then intern := intern - "00001"; end if;


output<= intern(3)&intern(2)&intern(1)&intern(0);
cola_1 <= cola1;
cola_2 <= cola2;
error <= std_err;
to_register <= to_reg;
end process;
END TypeArchitecture;

// VHDL entity registru_bancnote, as the project stores it:
LIBRARY ieee;
USE ieee.std_logic_1164.all;
use IEEE.STD_LOGIC_ARITH.ALL;
use IEEE.STD_LOGIC_UNSIGNED.ALL;

ENTITY registru_bancnote IS
  PORT (
     reset : in std_logic ;
     input_bancnote: in std_logic_vector ( 3 downto 0);
     bancnote_request :in std_logic_vector(3 downto 0);
     resurse1,resurse5 : out std_logic_vector (5 downto 0);
     bancnote_5_out, bancnote_1_out ,ledverde,ledrosu: out std_logic
     
    );
END registru_bancnote;


ARCHITECTURE TypeArchitecture OF registru_bancnote IS

BEGIN
process(input_bancnote,bancnote_request,reset)
variable nr_de_5 : std_logic_vector(5 downto 0) := "011111";
variable nr_de_1 : std_logic_vector(5 downto 0) :="011111";
variable b5out :std_logic :='0';
variable b1out :std_logic :='0';
variable flag : std_logic_vector (5 downto 0) := "011101";
variable a : std_logic := '0';
begin
b1out:='0';b5out:='0';
if(reset ='1' AND input_bancnote ="0000") then nr_de_5:= "011111"; nr_de_1 := "011111"; end if;

if(nr_de_5 < flag  OR nr_de_1 <flag) then a:= '0'; 
else a :='1'; end if;

if(bancnote_request = "0001") then nr_de_1 := nr_de_1 -"000001"; b1out:='1'; b5out:='0'; 
elsif(bancnote_request = "0101") then nr_de_5 := nr_de_5 - "000001"; b1out:='0'; b5out:='1'; end if;

if(input_bancnote = "0001") then nr_de_1 := nr_de_1 + "000001"; 
elsif(input_bancnote = "0101") then nr_de_5 := nr_de_5 + "000001"; end if;

bancnote_5_out <= b5out;
bancnote_1_out <= b1out;
resurse5 <= nr_de_5;
resurse1 <= nr_de_1;
ledverde <= a;
ledrosu <= not a ;
end process;

END TypeArchitecture;

// VHDL entity SevenSegmentDecoder, as the project stores it:
library ieee;
use ieee.std_logic_1164.all;
use ieee.numeric_std.all;

entity SevenSegmentDecoder is
  port (
    Input: in std_logic_vector(3 downto 0);
    
    output1 : out std_logic_vector(6 downto 0);
    output2 :out std_logic_vector(6 downto 0)

  );
end entity SevenSegmentDecoder;

architecture Behavioral of SevenSegmentDecoder is
begin

  process(Input)
    variable Value0: integer range 0 to 15;
   
  begin
    Value0 := to_integer(unsigned(Input(3 downto 0)));
   
    
    case Value0 is
      when 0 => output1 <= "1111110"; output2 <= "1111110";
      when 1 => output1 <= "0110000";output2 <= "1111110";
      when 2 => output1 <= "1101101";output2 <= "1111110";
      when 3 => output1 <= "1111001";output2 <= "1111110";
      when 4 => output1 <= "0110011";output2 <= "1111110";
      
      when 5 => output1 <= "1011011";output2 <= "1111110";
      when 6 => output1 <= "1011111";output2 <= "1111110";
      
      when 7 => output1 <= "1110000";output2 <= "1111110";
      when 8 => output1 <= "1111111";output2 <= "1111110";
      when 9 => output1 <= "1111011";output2 <= "1111110";
      
      when 10 => output2 <= "0110000"; output1 <= "1111110";
      when 11 => output2 <="0110000"; output1 <="0110000";
      when 12 => output2 <="0110000"; output1 <="1101101";
      when 13 =>output2 <="0110000"; output1 <="1111001";
      when 14 =>output2<="0110000";output1 <="0110011";
      when 15=>output2<="0110000";output1 <="1011011";

      
    end case;
    end process;
    end architecture;

// VHDL entity ALU, as the project stores it:
LIBRARY ieee;
USE ieee.std_logic_1164.all;
use IEEE.STD_LOGIC_ARITH.ALL;
use IEEE.STD_LOGIC_UNSIGNED.ALL;

ENTITY ALU IS
  PORT (
     clk ,vreaurest,OK: in std_logic;
     input_credit : in  std_logic_vector(3 downto 0);
     output_request : out std_logic_vector(3 downto 0);
     semnal_reset ,disable: out std_logic
    );
END ALU;



ARCHITECTURE TypeArchitecture OF ALU IS

BEGIN
process(clk,vreaurest)
variable sum : std_logic_vector (3 downto 0) := "0000";
variable req : std_logic_vector (3 downto 0) := "0000";
variable cntrl : integer := 0;
variable smn : std_logic := '0';
variable in_process : std_logic := '0';
variable enable_intern : std_logic := '1';
variable delay : integer := 0 ;
begin

if(vreaurest='1' AND enable_intern = '1' AND OK ='1') then 
sum := input_credit ;in_process := '1'; enable_intern := '0' ;end if;
if(rising_edge(clk))  
then  
    if( sum > 4 ) then req := "0101" ; sum := sum -5 ;cntrl := cntrl +1; in_process := '1';  
elsif(sum <5  AND sum >0) then req :="0001" ; sum := sum -1;cntrl := cntrl +1;  in_process := '1'; 
end if;  
end if;  

if(falling_edge(clk)) then req := "0000"; smn :='0'; end if;
output_request <= req;
if(sum = "0000" and cntrl /= 0) then smn := '1'; in_process:= '0';enable_intern :='1'; end if;

if(falling_edge(clk)) then smn :='0' ;cntrl :=0; end if;
semnal_reset <= smn;
disable <= not in_process;
end process;

END TypeArchitecture;

// VHDL entity FrequencyDivider, as the project stores it:
LIBRARY ieee;
USE ieee.std_logic_1164.all;
use ieee.std_logic_unsigned.all;

ENTITY FrequencyDivider IS
  PORT (
Clock: in std_logic;
		clk_1hz: out std_logic
    );
END FrequencyDivider;


ARCHITECTURE TypeArchitecture OF FrequencyDivider IS
BEGIN
process (clock)
	variable  var: std_logic_vector  (3 downto 0) := (others =>'0');
	begin
		if rising_edge (clock) then
			
				var:=var+1;
		
		end if;
	clk_1hz <= var(3);
end process;
END TypeArchitecture;

// VHDL entity d_ff, as the project stores it:
LIBRARY ieee;
USE ieee.std_logic_1164.all;

ENTITY d_ff IS
  PORT (
  D,CLK : in std_logic;
  Q:out std_logic
    );
END d_ff;
ARCHITECTURE TypeArchitecture OF d_ff IS
BEGIN
process(CLK)
begin
if(rising_edge(clk)) then 
Q<='0';
else
Q<=D;
end if;
end process;
END TypeArchitecture;

// VHDL entity main_vending, as the project stores it:
--------------------------------------------------------------------------------
-- Project : Vending machine
-- File    :
-- Autor   : Armega Andrei 321CC  , Alexandra Manloache 321CC , Elena Dulgheru 324CA
-- Date    : 12/14/2023
--

LIBRARY ieee;
USE ieee.std_logic_1164.all;

ENTITY main_vending IS
  PORT (
  bancnota_1_leu , bancnota_5_leu, bancnota_10_leu ,cola ,pepsi,clk,rest,RESETDEV: in std_logic ;
  bancnote_5_in_memorie , bancnote_1_in_memorie : out  std_logic_vector (5 downto 0);
  rest5_catre_utilizator ,rest1_catre_utilizator ,se_poate_da_rest , nu_se_poate_da_rest :out std_logic;
   eliberare_cola,eliberare_pepsi ,respingere_bancnota: out std_logic;
   credit : out std_logic_vector (3 downto 0) 
    );
END main_vending;


ARCHITECTURE TypeArchitecture OF main_vending IS
component decodificator IS
  PORT (
    input1,input2,input3 : in std_logic;
    semnal_out : out std_logic_vector (3 downto 0)
    );
END component;

component calculator IS
  PORT (
 input : in std_logic_vector(3 downto 0);
   reset,vreaucola,vreaucola2,vreaurest,enable: in std_logic;
   cola_1 ,cola_2:out std_logic;
   output ,to_register:out std_logic_vector(3 downto 0);
   error :out std_logic
    );
END component;

component registru_bancnote IS
  PORT (
     reset : in std_logic ;
     input_bancnote: in std_logic_vector ( 3 downto 0);
     bancnote_request :in std_logic_vector(3 downto 0);
     resurse1,resurse5 : out std_logic_vector (5 downto 0);
     bancnote_5_out, bancnote_1_out ,ledverde,ledrosu: out std_logic
     
    );
END component;
component ALU IS
  PORT (
     clk ,vreaurest,OK: in std_logic;
     input_credit : in  std_logic_vector(3 downto 0);
     output_request : out std_logic_vector(3 downto 0);
     semnal_reset ,disable: out std_logic
    );
END component;

component FrequencyDivider IS
  PORT (
Clock: in std_logic;
		clk_1hz: out std_logic
    );
END component;

component d_ff IS
  PORT (
  D,CLK : in std_logic;
  Q:out std_logic
    );
END component;


signal decodificator_to_calculator : std_logic_vector (3 downto 0) := "0000";
signal ALU_to_calc_reset : std_logic := '0';
signal ALU_to_calc_enable : std_logic := '0';
signal output_from_calc :std_logic_vector (3 downto 0) := "0000";
signal to_register_signal:std_logic_vector (3 downto 0) := "0000";
signal clk_1_hertz ,q: std_logic :='0';
signal ALU_to_register :std_logic_vector (3 downto 0) := "0000";
signal for_green :std_logic :='0';
BEGIN

decod : decodificator port map (bancnota_1_leu , bancnota_5_leu, bancnota_10_leu,decodificator_to_calculator);
calc : calculator port map (decodificator_to_calculator , ALU_to_calc_reset,cola,pepsi,rest,ALU_to_calc_enable,eliberare_cola,eliberare_pepsi,output_from_calc,to_register_signal,respingere_bancnota);
div : FrequencyDivider port map (clk ,clk_1_hertz);
reg : registru_bancnote port map (RESETDEV,to_register_signal,ALU_to_register, bancnote_1_in_memorie,bancnote_5_in_memorie,rest5_catre_utilizator ,rest1_catre_utilizator,for_green, nu_se_poate_da_rest);
ff : d_ff port map(rest,clk,q);
aluu : alu port map (clk_1_hertz,q,for_green,output_from_calc,ALU_to_register ,ALU_to_calc_reset ,ALU_to_calc_enable);
se_poate_da_rest <= for_green;
credit <= output_from_calc;
END TypeArchitecture;
------------------------

LIBRARY ieee;
USE ieee.std_logic_1164.all;

ENTITY decodificator IS
  PORT (
    input1,input2,input3 : in std_logic;
    semnal_out : out std_logic_vector (3 downto 0)
    );
END decodificator;


ARCHITECTURE TypeArchitecture OF decodificator IS

BEGIN

process(input1,input2,input3)
variable to_out: std_logic_vector (3 downto 0) := "0000";
begin


if( input1 = '1' AND  input2 ='0' AND input3 ='0') then
to_out := "0001";
elsif (input1 ='0'AND input2 = '1' AND input3 ='0') then
to_out :="0101";
elsif (input1 ='0' AND input2 = '0' AND input3 ='1')then
to_out :="1010";
elsif (input1 ='0' AND input2 = '0' AND input3 ='0')then
to_out:="0000";
end if;
semnal_out <= to_out;
end process;

END TypeArchitecture;


LIBRARY ieee;
USE ieee.std_logic_1164.all;
use IEEE.STD_LOGIC_ARITH.ALL;
use IEEE.STD_LOGIC_UNSIGNED.ALL;

ENTITY calculator IS
  PORT (
 input : in std_logic_vector(3 downto 0);
   reset,vreaucola,vreaucola2,vreaurest,enable: in std_logic;
   cola_1 ,cola_2:out std_logic;
   output ,to_register:out std_logic_vector(3 downto 0);
   error :out std_logic
    );
END calculator;


ARCHITECTURE TypeArchitecture OF calculator IS

BEGIN

process(input,reset,vreaucola,vreaucola2,vreaurest)
variable intern : std_logic_vector(4 downto 0) := "00000";
variable std_err:std_logic :='0';
variable cola1 :std_logic :='0';
variable cola2 :std_logic :='0';
variable nr_bauturi : integer :=0;
variable req : std_logic_vector (3 downto 0) := "0000";
variable to_reg : std_logic_vector (3 downto 0) :="0000";

begin
if(input /= "0000" AND enable ='0') then std_err := '1'; end if;

if(input + intern < "10000" AND enable ='1') then intern := intern +input;cola1 :='0'; cola2:='0'; std_err :='0';to_reg := input;
elsif (input+intern >"01111") then std_err :='1'; 
else std_err :='0'; end if;

if( vreaucola ='1' AND intern > "00010" AND vreaucola2 ='0' AND reset ='0'  AND enable ='1') 
then intern := intern - "00011";
cola1 :='1';cola2:='0';
nr_bauturi := nr_bauturi+1; 
std_err :='0';
end if;

if( vreaucola2 ='1' AND intern > "00011" AND vreaucola ='0' AND reset ='0'  AND enable ='1') 
then intern := intern - "00100";
cola2 :='1'; cola1:='0';
nr_bauturi := nr_bauturi+1;
std_err :='0';
end if;

if(reset ='1') 
then intern :="00000"; 
cola1 :='0'; cola2 :='0';
std_err :='0';	
end if;

 if( vreaurest = '1'AND vreaucola2 ='0' AND vreaucola='0'  AND nr_bauturi =0 AND intern > "01001") then intern := intern - "00001"; end if;


output<= intern(3)&intern(2)&intern(1)&intern(0);
cola_1 <= cola1;
cola_2 <= cola2;
error <= std_err;
to_register <= to_reg;
end process;
END TypeArchitecture;



LIBRARY ieee;
USE ieee.std_logic_1164.all;

use IEEE.STD_LOGIC_ARITH.ALL;
use IEEE.STD_LOGIC_UNSIGNED.ALL;

ENTITY registru_bancnote IS
  PORT (
     reset : in std_logic ;
     input_bancnote: in std_logic_vector ( 3 downto 0);
     bancnote_request :in std_logic_vector(3 downto 0);
     resurse1,resurse5 : out std_logic_vector (5 downto 0);
     bancnote_5_out, bancnote_1_out ,ledverde,ledrosu: out std_logic
     
    );
END registru_bancnote;


ARCHITECTURE TypeArchitecture OF registru_bancnote IS

BEGIN

process(input_bancnote,bancnote_request,reset)
variable nr_de_5 : std_logic_vector(5 downto 0) := "011111";
variable nr_de_1 : std_logic_vector(5 downto 0) :="011111";
variable b5out :std_logic :='0';
variable b1out :std_logic :='0';
variable flag : std_logic_vector (5 downto 0) := "011101";
variable a : std_logic := '0';
begin
b1out:='0';b5out:='0';
if(reset ='1' AND input_bancnote ="0000") then nr_de_5:= "011111"; nr_de_1 := "011111"; end if;

if(nr_de_5 < flag  OR nr_de_1 <flag) then a:= '0'; 
else a :='1'; end if;

if(bancnote_request = "0001") then nr_de_1 := nr_de_1 -"000001"; b1out:='1'; b5out:='0'; 
elsif(bancnote_request = "0101") then nr_de_5 := nr_de_5 - "000001"; b1out:='0'; b5out:='1'; end if;

if(input_bancnote = "0001") then nr_de_1 := nr_de_1 + "000001"; 
elsif(input_bancnote = "0101") then nr_de_5 := nr_de_5 + "000001"; end if;

bancnote_5_out <= b5out;
bancnote_1_out <= b1out;
resurse5 <= nr_de_5;
resurse1 <= nr_de_1;
ledverde <= a;
ledrosu <= not a ;
end process;

END TypeArchitecture;

LIBRARY ieee;
USE ieee.std_logic_1164.all;

use IEEE.STD_LOGIC_ARITH.ALL;
use IEEE.STD_LOGIC_UNSIGNED.ALL;

ENTITY ALU IS
  PORT (
     clk ,vreaurest,OK: in std_logic;
     input_credit : in  std_logic_vector(3 downto 0);
     output_request : out std_logic_vector(3 downto 0);
     semnal_reset ,disable: out std_logic
    );
END ALU;



ARCHITECTURE TypeArchitecture OF ALU IS

BEGIN

process(clk,vreaurest)
variable sum : std_logic_vector (3 downto 0) := "0000";
variable req : std_logic_vector (3 downto 0) := "0000";
variable cntrl : integer := 0;
variable smn : std_logic := '0';
variable in_process : std_logic := '0';
variable enable_intern : std_logic := '1';
variable delay : integer := 0 ;
begin
if(vreaurest='1' AND enable_intern = '1' AND OK ='1') then 

sum := input_credit ;in_process := '1'; enable_intern := '0' ;end if;

  
if(rising_edge(clk))  
then  
    if( sum > 4 ) then req := "0101" ; sum := sum -5 ;cntrl := cntrl +1; in_process := '1';  
elsif(sum <5  AND sum >0) then req :="0001" ; sum := sum -1;cntrl := cntrl +1;  in_process := '1'; 
end if;  
 
end if;  

if(falling_edge(clk)) then req := "0000"; smn :='0'; end if;
output_request <= req;
if(sum = "0000" and cntrl /= 0) then smn := '1'; in_process:= '0';enable_intern :='1'; end if;

if(falling_edge(clk)) then smn :='0' ;cntrl :=0; end if;
semnal_reset <= smn;
disable <= not in_process;
end process;
END TypeArchitecture;

LIBRARY ieee;
USE ieee.std_logic_1164.all;
use ieee.std_logic_unsigned.all;

ENTITY FrequencyDivider IS
  PORT (
Clock: in std_logic;
		clk_1hz: out std_logic
    );
END FrequencyDivider;


ARCHITECTURE TypeArchitecture OF FrequencyDivider IS
BEGIN
process (clock)
	variable  var: std_logic_vector  (3 downto 0) := (others =>'0');
	begin
		if rising_edge (clock) then
			
				var:=var+1;
		
		end if;
	clk_1hz <= var(3);
end process;
END TypeArchitecture;
LIBRARY ieee;
USE ieee.std_logic_1164.all;

ENTITY d_ff IS
  PORT (
  D,CLK : in std_logic;
  Q:out std_logic
    );
END d_ff;
ARCHITECTURE TypeArchitecture OF d_ff IS
BEGIN
process(CLK)
begin
if(rising_edge(clk)) then 
Q<='0';
else
Q<=D;
end if;
end process;
END TypeArchitecture;
